// Logisim project DepProject.circ as structural Verilog
module _1_bit_adder (
  input  A,
  input  B,
  input  CIN,
  output SUM,
  output COUT
);

  wire and_1_out, and_2_out, xor_1_out;

  xor xor_1 (xor_1_out, A, B);
  and and_1 (and_1_out, B, A);
  xor xor_2 (SUM, xor_1_out, CIN);
  and and_2 (and_2_out, xor_1_out, CIN);
  or or_1 (COUT, and_2_out, and_1_out);
endmodule

module _1_bit_ALU (
  input  A,
  input  B,
  input  CIN,
  input  C1,
  input  C2,
  output COUT,
  output OUTPUT
);

  wire and_1_out, multiplexer_1_out, n1_bit_adder_1_sum, or_1_out;

  and and_1 (and_1_out, A, B);
  or or_1 (or_1_out, A, B);
  _1_bit_adder u_1_bit_adder_1 (.A(A), .B(B), .CIN(CIN), .SUM(n1_bit_adder_1_sum), .COUT(COUT));
  Multiplexer multiplexer_1 (.in0(and_1_out), .in1(or_1_out), .out(multiplexer_1_out), .sel(C1));  // open: en
  Multiplexer multiplexer_2 (.in0(n1_bit_adder_1_sum), .in1(multiplexer_1_out), .out(OUTPUT), .sel(C2));  // open: en
endmodule

module _8_bit_ALU (
  input  A,
  input  in_2,
  input  in_3,
  input  in_4,
  input  in_5,
  input  in_6,
  input  in_7,
  input  in_8,
  input  B,
  input  in_10,
  input  in_11,
  input  in_12,
  input  in_13,
  input  in_14,
  input  in_15,
  input  in_16,
  input  CIN,
  input  C1,
  input  C2,
  output B0,
  output B1,
  output B2,
  output B3,
  output B4,
  output B5,
  output B6,
  output B7
);

  wire n1_bit_alu_1_cout, n1_bit_alu_2_cout, n1_bit_alu_3_cout, n1_bit_alu_4_cout, n1_bit_alu_5_cout,
       n1_bit_alu_6_cout, n1_bit_alu_7_cout;

  _1_bit_ALU u_1_bit_alu_1 (.A(A), .B(B), .CIN(CIN), .C1(C1), .C2(C2), .COUT(n1_bit_alu_1_cout), .OUTPUT(B0));
  _1_bit_ALU u_1_bit_alu_2 (
    .A(in_2), .B(in_10), .CIN(n1_bit_alu_1_cout), .C1(C1), .C2(C2), .COUT(n1_bit_alu_2_cout), .OUTPUT(B1));
  _1_bit_ALU u_1_bit_alu_3 (
    .A(in_3), .B(in_11), .CIN(n1_bit_alu_2_cout), .C1(C1), .C2(C2), .COUT(n1_bit_alu_3_cout), .OUTPUT(B2));
  _1_bit_ALU u_1_bit_alu_4 (
    .A(in_4), .B(in_12), .CIN(n1_bit_alu_3_cout), .C1(C1), .C2(C2), .COUT(n1_bit_alu_4_cout), .OUTPUT(B3));
  _1_bit_ALU u_1_bit_alu_5 (
    .A(in_5), .B(in_13), .CIN(n1_bit_alu_4_cout), .C1(C1), .C2(C2), .COUT(n1_bit_alu_5_cout), .OUTPUT(B4));
  _1_bit_ALU u_1_bit_alu_6 (
    .A(in_6), .B(in_14), .CIN(n1_bit_alu_5_cout), .C1(C1), .C2(C2), .COUT(n1_bit_alu_6_cout), .OUTPUT(B5));
  _1_bit_ALU u_1_bit_alu_7 (
    .A(in_7), .B(in_15), .CIN(n1_bit_alu_6_cout), .C1(C1), .C2(C2), .COUT(n1_bit_alu_7_cout), .OUTPUT(B6));
  _1_bit_ALU u_1_bit_alu_8 (.A(in_8), .B(in_16), .CIN(n1_bit_alu_7_cout), .C1(C1), .C2(C2), .OUTPUT(B7));  // open: COUT
endmodule

module _1_bit_ALU_Subtract (
  input  in_1,
  input  A,
  input  B,
  input  CIN,
  input  C1,
  input  C2,
  output COUT,
  output OUTPUT
);

  wire and_1_out, and_2_out, and_3_out, multiplexer_1_out, multiplexer_2_out, multiplexer_3_out,
       n1_bit_adder_1_sum, not_1_out, or_1_out, or_2_out, xor_1_out;

  and and_1 (and_1_out, A, B);
  or or_1 (or_1_out, A, B);
  not not_1 (not_1_out, B);
  _1_bit_adder u_1_bit_adder_1 (.A(A), .B(B), .CIN(CIN), .SUM(n1_bit_adder_1_sum), .COUT(COUT));
  Multiplexer multiplexer_1 (.in0(and_1_out), .in1(or_1_out), .out(multiplexer_1_out), .sel(C1));  // open: en
  Multiplexer multiplexer_2 (.in0(B), .in1(not_1_out), .out(multiplexer_2_out), .sel(in_1));  // open: en
  Multiplexer multiplexer_3 (.in0(or_2_out), .in1(n1_bit_adder_1_sum), .out(multiplexer_3_out), .sel(C1));  // open: en
  Multiplexer multiplexer_4 (.in0(multiplexer_3_out), .in1(multiplexer_1_out), .out(OUTPUT), .sel(C2));  // open: en
  xor xor_1 (xor_1_out, A, multiplexer_2_out);
  and and_2 (and_2_out, multiplexer_2_out, A);
  and and_3 (and_3_out, xor_1_out, CIN);
  or or_2 (or_2_out, and_3_out, and_2_out);
endmodule

module _8_bit_ALU_Subtract (
  input  A,
  input  in_2,
  input  in_3,
  input  in_4,
  input  in_5,
  input  in_6,
  input  in_7,
  input  in_8,
  input  B,
  input  in_10,
  input  in_11,
  input  in_12,
  input  in_13,
  input  in_14,
  input  in_15,
  input  in_16,
  input  CIN,
  input  C1,
  input  C2,
  output B0,
  output B1,
  output B2,
  output B3,
  output B4,
  output B5,
  output B6,
  output B7
);

  wire n1_bit_alu_subtract_1_cout, n1_bit_alu_subtract_2_cout, n1_bit_alu_subtract_3_cout,
       n1_bit_alu_subtract_4_cout, n1_bit_alu_subtract_5_cout, n1_bit_alu_subtract_6_cout,
       n1_bit_alu_subtract_7_cout;

  _1_bit_ALU_Subtract u_1_bit_alu_subtract_1 (
    .A(A), .B(B), .CIN(CIN), .C1(C1), .C2(C2), .COUT(n1_bit_alu_subtract_1_cout), .OUTPUT(B0));  // open: in_1
  _1_bit_ALU_Subtract u_1_bit_alu_subtract_2 (
    .A(in_2), .B(in_10), .CIN(n1_bit_alu_subtract_1_cout), .C1(C1), .C2(C2),
    .COUT(n1_bit_alu_subtract_2_cout), .OUTPUT(B1));  // open: in_1
  _1_bit_ALU_Subtract u_1_bit_alu_subtract_3 (
    .A(in_3), .B(in_11), .CIN(n1_bit_alu_subtract_2_cout), .C1(C1), .C2(C2),
    .COUT(n1_bit_alu_subtract_3_cout), .OUTPUT(B2));  // open: in_1
  _1_bit_ALU_Subtract u_1_bit_alu_subtract_4 (
    .A(in_4), .B(in_12), .CIN(n1_bit_alu_subtract_3_cout), .C1(C1), .C2(C2),
    .COUT(n1_bit_alu_subtract_4_cout), .OUTPUT(B3));  // open: in_1
  _1_bit_ALU_Subtract u_1_bit_alu_subtract_5 (
    .A(in_5), .B(in_13), .CIN(n1_bit_alu_subtract_4_cout), .C1(C1), .C2(C2),
    .COUT(n1_bit_alu_subtract_5_cout), .OUTPUT(B4));  // open: in_1
  _1_bit_ALU_Subtract u_1_bit_alu_subtract_6 (
    .A(in_6), .B(in_14), .CIN(n1_bit_alu_subtract_5_cout), .C1(C1), .C2(C2),
    .COUT(n1_bit_alu_subtract_6_cout), .OUTPUT(B5));  // open: in_1
  _1_bit_ALU_Subtract u_1_bit_alu_subtract_7 (
    .A(in_7), .B(in_15), .CIN(n1_bit_alu_subtract_6_cout), .C1(C1), .C2(C2),
    .COUT(n1_bit_alu_subtract_7_cout), .OUTPUT(B6));  // open: in_1
  _1_bit_ALU_Subtract u_1_bit_alu_subtract_8 (
    .A(in_8), .B(in_16), .CIN(n1_bit_alu_subtract_7_cout), .C1(C1), .C2(C2), .OUTPUT(B7));  // open: in_1, COUT
endmodule

module Register_File (
  input  [3:0] rd,
  input  [3:0] rs1,
  input  [3:0] in_3,
  input  [7:0] Write_Input,
  input  Enable,
  input  Clock,
  output [7:0] out_7,
  output [7:0] out_8
);

  wire and_1_out, and_2_out, and_3_out, and_4_out, and_5_out, and_6_out, and_7_out, and_8_out, and_9_out,
       and_10_out, and_11_out, and_12_out, and_13_out, and_14_out, and_15_out, and_16_out, decoder_1_out0,
       decoder_1_out1, decoder_1_out2, decoder_1_out3, decoder_1_out4, decoder_1_out5, decoder_1_out6,
       decoder_1_out7, decoder_1_out8, decoder_1_out9, decoder_1_out10, decoder_1_out11, decoder_1_out12,
       decoder_1_out13, decoder_1_out14, decoder_1_out15;
  wire [7:0] register_1_q, register_2_q, register_3_q, register_4_q, register_5_q, register_6_q,
       register_7_q, register_8_q, register_9_q, register_10_q, register_11_q, register_12_q, register_13_q,
       register_14_q, register_15_q, register_16_q;

  Decoder #(.select(4)) decoder_1 (
    .out0(decoder_1_out0), .out1(decoder_1_out1), .out2(decoder_1_out2), .out3(decoder_1_out3),
    .out4(decoder_1_out4), .out5(decoder_1_out5), .out6(decoder_1_out6), .out7(decoder_1_out7),
    .out8(decoder_1_out8), .out9(decoder_1_out9), .out10(decoder_1_out10), .out11(decoder_1_out11),
    .out12(decoder_1_out12), .out13(decoder_1_out13), .out14(decoder_1_out14), .out15(decoder_1_out15),
    .sel(rd));  // open: en
  and and_1 (and_1_out, decoder_1_out0, Enable);
  and and_2 (and_2_out, decoder_1_out1, Enable);
  and and_3 (and_3_out, decoder_1_out2, Enable);
  and and_4 (and_4_out, decoder_1_out3, Enable);
  and and_5 (and_5_out, decoder_1_out4, Enable);
  and and_6 (and_6_out, decoder_1_out5, Enable);
  and and_7 (and_7_out, decoder_1_out6, Enable);
  and and_8 (and_8_out, decoder_1_out7, Enable);
  Register register_1 (.D(Write_Input), .en(and_1_out), .Q(register_1_q), .clk(Clock));  // open: clr
  Register register_2 (.D(Write_Input), .en(and_2_out), .Q(register_2_q), .clk(Clock));  // open: clr
  Register register_3 (.D(Write_Input), .en(and_3_out), .Q(register_3_q), .clk(Clock));  // open: clr
  Register register_4 (.D(Write_Input), .en(and_4_out), .Q(register_4_q), .clk(Clock));  // open: clr
  Register register_5 (.D(Write_Input), .en(and_5_out), .Q(register_5_q), .clk(Clock));  // open: clr
  Register register_6 (.D(Write_Input), .en(and_6_out), .Q(register_6_q), .clk(Clock));  // open: clr
  Register register_7 (.D(Write_Input), .en(and_7_out), .Q(register_7_q), .clk(Clock));  // open: clr
  Register register_8 (.D(Write_Input), .en(and_8_out), .Q(register_8_q), .clk(Clock));  // open: clr
  and and_9 (and_9_out, decoder_1_out8, Enable);
  and and_10 (and_10_out, decoder_1_out9, Enable);
  and and_11 (and_11_out, decoder_1_out10, Enable);
  and and_12 (and_12_out, decoder_1_out11, Enable);
  and and_13 (and_13_out, decoder_1_out12, Enable);
  and and_14 (and_14_out, decoder_1_out13, Enable);
  and and_15 (and_15_out, decoder_1_out14, Enable);
  and and_16 (and_16_out, decoder_1_out15, Enable);
  Register register_9 (.D(Write_Input), .en(and_9_out), .Q(register_9_q), .clk(Clock));  // open: clr
  Register register_10 (.D(Write_Input), .en(and_10_out), .Q(register_10_q), .clk(Clock));  // open: clr
  Register register_11 (.D(Write_Input), .en(and_11_out), .Q(register_11_q), .clk(Clock));  // open: clr
  Register register_12 (.D(Write_Input), .en(and_12_out), .Q(register_12_q), .clk(Clock));  // open: clr
  Register register_13 (.D(Write_Input), .en(and_13_out), .Q(register_13_q), .clk(Clock));  // open: clr
  Register register_14 (.D(Write_Input), .en(and_14_out), .Q(register_14_q), .clk(Clock));  // open: clr
  Register register_15 (.D(Write_Input), .en(and_15_out), .Q(register_15_q), .clk(Clock));  // open: clr
  Register register_16 (.D(Write_Input), .en(and_16_out), .Q(register_16_q), .clk(Clock));  // open: clr
  Multiplexer #(.select(4), .width(8)) multiplexer_1 (
    .in0(register_1_q), .in1(register_2_q), .in2(register_3_q), .in3(register_4_q), .in4(register_5_q),
    .in5(register_6_q), .in6(register_7_q), .in7(register_8_q), .in8(register_9_q), .in9(register_10_q),
    .in10(register_11_q), .in11(register_12_q), .in12(register_13_q), .in13(register_14_q),
    .in14(register_15_q), .in15(register_16_q), .out(out_7), .sel(rs1));  // open: en
  Multiplexer #(.select(4), .width(8)) multiplexer_2 (
    .in0(register_1_q), .in1(register_2_q), .in2(register_3_q), .in3(register_4_q), .in4(register_5_q),
    .in5(register_6_q), .in6(register_7_q), .in7(register_8_q), .in8(register_9_q), .in9(register_10_q),
    .in10(register_11_q), .in11(register_12_q), .in12(register_13_q), .in13(register_14_q),
    .in14(register_15_q), .in15(register_16_q), .out(out_8), .sel(in_3));  // open: en

  // Notes on the sheet:
  //   rs2
endmodule

module Test (
  input  Input_A,
  input  [3:0] rd,
  input  Input_B,
  input  [3:0] rs1,
  input  Carry_In,
  input  [3:0] rs2,
  input  C1__Setting_1,
  input  [7:0] in_8,
  input  C2__Setting_2,
  input  Enable,
  input  Clock,
  input  in_12,
  input  Input_A_Bit_1,
  input  in_14,
  input  Input_A_Bit_2,
  input  in_16,
  input  Input_A_Bit_3,
  input  Input_A_Bit_4,
  input  Input_A_Bit_1_2,
  input  Input_A_Bit_5,
  input  Input_A_Bit_2_2,
  input  Input_A_Bit_6,
  input  Input_A_Bit_3_2,
  input  Input_A_Bit_7,
  input  Input_B_Bit_1,
  input  in_26,
  input  Input_A_Bit_8,
  input  Input_B_Bit_2,
  input  in_29,
  input  Input_B_Bit_1_2,
  input  Input_B_Bit_3,
  input  in_32,
  input  Input_B_Bit_2_2,
  input  Input_B_Bit_3_2,
  input  Input_B_Bit_4,
  input  Carry_In__0,
  input  Input_B_Bit_5,
  input  C1,
  input  [3:0] opcode,
  input  Input_B_Bit_6,
  input  C2,
  input  Input_B_Bit_7,
  input  Input_B_Bit_8,
  output out_44,
  output Carry_Out,
  output Output,
  output out_47,
  output [7:0] out_48,
  output out_49,
  output out_50,
  output out_51,
  output out_52,
  output out_53,
  output out_54,
  output out_55,
  output out_56,
  output out_57,
  output out_58,
  output out_59,
  output out_60
);

  wire [2:0] register_1_q, undriven;
  wire [6:1] register_file_1_p7;
  wire [15:0] ram_2_data;

  Register #(.width(3)) register_1 (.D(undriven), .Q(register_1_q));  // open: en, clk, clr
  // Register_File register_file_1: pin names not known; wires that end beside it: rd, rs1, rs2, in_8, Enable, Clock, {out_47, register_file_1_p7, out_44}, out_48
  _8_bit_ALU u_8_bit_alu_1 (
    .A(Input_A_Bit_1), .in_2(Input_A_Bit_2), .in_3(Input_A_Bit_3), .in_4(Input_A_Bit_4),
    .in_5(Input_A_Bit_5), .in_6(Input_A_Bit_6), .in_7(Input_A_Bit_7), .in_8(Input_A_Bit_8),
    .B(Input_B_Bit_1_2), .in_10(Input_B_Bit_2_2), .in_11(Input_B_Bit_3_2), .in_12(Input_B_Bit_4),
    .in_13(Input_B_Bit_5), .in_14(Input_B_Bit_6), .in_15(Input_B_Bit_7), .in_16(Input_B_Bit_8),
    .CIN(Carry_In__0), .C1(C1), .C2(C2), .B0(out_50), .B1(out_51), .B2(out_52), .B3(out_54), .B4(out_56),
    .B5(out_58), .B6(out_59), .B7(out_60));
  RAM #(.bus("separate")) ram_1 ();  // open: addr, din, data, str, sel, clk, ld, clr
  RAM #(.addrWidth(3), .dataWidth(16), .bus("separate")) ram_2 (
    .addr(register_1_q), .data(ram_2_data));  // open: din, str, sel, clk, ld, clr
  Multiplexer multiplexer_1 (.in0(in_12), .in1(in_14), .out(out_49), .sel(in_16));  // open: en
  _1_bit_ALU u_1_bit_alu_1 (
    .A(Input_A), .B(Input_B), .CIN(Carry_In), .C1(C1__Setting_1), .C2(C2__Setting_2), .COUT(Carry_Out),
    .OUTPUT(Output));
  _3_bit_ALU u_3_bit_alu_1 (
    .A(Input_A_Bit_1_2), .in_2(Input_A_Bit_2_2), .in_3(Input_A_Bit_3_2), .B(Input_B_Bit_1),
    .in_5(Input_B_Bit_2), .in_6(Input_B_Bit_3), .CIN(in_26), .C1(in_29), .C2(in_32), .B0(out_53),
    .B1(out_55), .B2(out_57));

  // Notes on the sheet:
  //   Write Input
  //   add 1 with 3 bit ALU
  //   add 5 when branching
  //   Bits: 1 is last digit, 8 is first digit 
  //   00: Add
  //   01: AND
  //   10: Add
  //   11: OR
  //   rs1 Output
  //   rs2 Output
  //   don't need
  //   make Instr Memory add imd (5)
  //   turn on load in data memory
  //   turn on add in ALU  (00/10)
endmodule

module Computer (
  input  in_1,
  input  in_2,
  input  in_3,
  input  in_4,
  input  [2:0] in_5,
  input  in_6,
  input  in_7,
  input  in_8,
  input  in_9,
  input  in_10,
  input  in_11,
  input  in_12,
  output [7:0] out_13,
  output [7:0] Write_Input,
  output [7:0] out_15,
  output [7:0] out_16,
  output [3:0] rs1,
  output [3:0] rs2,
  output [3:0] rd,
  output out_20,
  output out_21,
  output out_22,
  output [3:0] imd_rs2,
  output [3:0] rs1_2,
  output [3:0] imd_rd,
  output [3:0] opcode
);

  wire multiplexer_3_out, multiplexer_4_out, not_1_out;
  wire [2:0] multiplexer_1_out, n3_bit_alu_1_b0, register_1_q;
  wire [7:0] n8_bit_alu_2_b0, n8_bit_alu_3_b0, ram_2_data;

  Multiplexer #(.width(3)) multiplexer_1 (
    .in0(in_5), .in1(imd_rd[2:0]), .out(multiplexer_1_out), .sel(opcode[0]));  // open: en
  Multiplexer #(.width(8)) multiplexer_2 (
    .in0(n8_bit_alu_3_b0), .in1(out_16), .out(Write_Input), .sel(opcode[2]));  // open: en
  _3_bit_ALU u_3_bit_alu_1 (
    .A(register_1_q[0]), .in_2(register_1_q[1]), .in_3(register_1_q[2]), .B(multiplexer_1_out[0]),
    .in_5(multiplexer_1_out[1]), .in_6(multiplexer_1_out[2]), .CIN(in_7), .C1(in_10), .C2(in_11),
    .B0(n3_bit_alu_1_b0[0]), .B1(n3_bit_alu_1_b0[1]), .B2(n3_bit_alu_1_b0[2]));
  not not_1 (not_1_out, in_6);
  Register #(.width(3)) register_1 (.D(n3_bit_alu_1_b0), .Q(register_1_q), .clk(in_6));  // open: en, clr
  Register_File register_file_1 (
    .rd(imd_rd), .rs1(rs1), .in_3(imd_rs2), .Write_Input(Write_Input), .Enable(in_1), .Clock(not_1_out),
    .out_7(out_13), .out_8(out_15));
  _8_bit_ALU u_8_bit_alu_1 (
    .A(out_13[0]), .in_2(out_13[1]), .in_3(out_13[2]), .in_4(out_13[3]), .in_5(out_13[4]), .in_6(out_13[5]),
    .in_7(out_13[6]), .in_8(out_13[7]), .B(out_15[0]), .in_10(out_15[1]), .in_11(out_15[2]),
    .in_12(out_15[3]), .in_13(out_15[4]), .in_14(out_15[5]), .in_15(out_15[6]), .in_16(out_15[7]),
    .CIN(in_2), .C1(multiplexer_3_out), .C2(multiplexer_3_out), .B0(out_16[0]), .B1(out_16[1]),
    .B2(out_16[2]), .B3(out_16[3]), .B4(out_16[4]), .B5(out_16[5]), .B6(out_16[6]), .B7(out_16[7]));
  RAM #(.addrWidth(3), .dataWidth(16), .bus("asynch")) ram_1 (
    .addr(register_1_q), .data({imd_rs2, rs1, imd_rd, opcode}), .ld(in_8));  // open: sel, clr
  Multiplexer multiplexer_3 (.in1(in_9), .out(multiplexer_3_out), .sel(opcode[2]));  // open: in0, en
  Multiplexer multiplexer_4 (.in1(in_12), .out(multiplexer_4_out), .sel(opcode[1]));  // open: in0, en
  _8_bit_ALU u_8_bit_alu_2 (
    .A(out_13[0]), .in_2(out_13[1]), .in_3(out_13[2]), .in_4(out_13[3]), .in_5(out_13[4]), .in_6(out_13[5]),
    .in_7(out_13[6]), .in_8(out_13[7]), .B(imd_rs2[0]), .in_10(imd_rs2[1]), .in_11(imd_rs2[2]),
    .in_12(imd_rs2[3]), .in_13(in_3), .in_14(in_3), .in_15(in_3), .in_16(in_3), .CIN(in_3),
    .C1(multiplexer_4_out), .C2(multiplexer_4_out), .B0(n8_bit_alu_2_b0[0]), .B1(n8_bit_alu_2_b0[1]),
    .B2(n8_bit_alu_2_b0[2]), .B3(n8_bit_alu_2_b0[3]), .B4(n8_bit_alu_2_b0[4]), .B5(n8_bit_alu_2_b0[5]),
    .B6(n8_bit_alu_2_b0[6]), .B7(n8_bit_alu_2_b0[7]));
  RAM #(.bus("separate")) ram_2 (
    .addr(n8_bit_alu_2_b0), .data(ram_2_data), .ld(opcode[1]));  // open: din, str, sel, clk, clr
  _8_bit_ALU u_8_bit_alu_3 (
    .A(ram_2_data[0]), .in_2(ram_2_data[1]), .in_3(ram_2_data[2]), .in_4(ram_2_data[3]),
    .in_5(ram_2_data[4]), .in_6(ram_2_data[5]), .in_7(ram_2_data[6]), .in_8(ram_2_data[7]), .B(imd_rs2[0]),
    .in_10(imd_rs2[1]), .in_11(imd_rs2[2]), .in_12(imd_rs2[3]), .in_13(in_4), .in_14(in_4), .in_15(in_4),
    .in_16(in_4), .CIN(in_4), .C1(in_4), .C2(in_4), .B0(n8_bit_alu_3_b0[0]), .B1(n8_bit_alu_3_b0[1]),
    .B2(n8_bit_alu_3_b0[2]), .B3(n8_bit_alu_3_b0[3]), .B4(n8_bit_alu_3_b0[4]), .B5(n8_bit_alu_3_b0[5]),
    .B6(n8_bit_alu_3_b0[6]), .B7(n8_bit_alu_3_b0[7]));

  assign out_20 = opcode[0];
  assign out_21 = opcode[1];
  assign out_22 = opcode[2];
  assign rd = imd_rd;
  assign rs1_2 = rs1;
  assign rs2 = imd_rs2;

  // Notes on the sheet:
  //   chooses load vs add
  //   add 5 to inst mem
  //   3 bit ALU (only add)
  //   Register File
  //   Instruction Memory
  //   8-bit ALU
  //   rs1 Output
  //   rs2 Output
  //   immediate for ld
  //   turn on add in ALU  (00/10)
  //   Sum of rs1 and rs2 Outputs
  //   turn on load in data memory
  //   Data Memory
  //   make Instr Memory add imd (5)
  //   turn on load in data memory
  //   turn on add in ALU  (00/10)
  //   8-bit ALU (only adds)
endmodule

module _3_bit_ALU (
  input  A,
  input  in_2,
  input  in_3,
  input  B,
  input  in_5,
  input  in_6,
  input  CIN,
  input  C1,
  input  C2,
  output B0,
  output B1,
  output B2
);

  wire n1_bit_alu_1_cout, n1_bit_alu_2_cout;

  _1_bit_ALU u_1_bit_alu_1 (.A(A), .B(B), .CIN(CIN), .C1(C1), .C2(C2), .COUT(n1_bit_alu_1_cout), .OUTPUT(B0));
  _1_bit_ALU u_1_bit_alu_2 (
    .A(in_2), .B(in_5), .CIN(n1_bit_alu_1_cout), .C1(C1), .C2(C2), .COUT(n1_bit_alu_2_cout), .OUTPUT(B1));
  _1_bit_ALU u_1_bit_alu_3 (.A(in_3), .B(in_6), .CIN(n1_bit_alu_2_cout), .C1(C1), .C2(C2), .OUTPUT(B2));  // open: COUT
endmodule

module Experimentation (
  input  in_1,
  input  in_2,
  input  in_3,
  input  [2:0] in_4,
  input  in_5,
  input  in_6,
  input  in_7,
  input  in_8,
  input  in_9,
  input  in_10,
  input  in_11,
  output [7:0] out_12,
  output [7:0] Write_Input,
  output [7:0] out_14,
  output [7:0] out_15,
  output [3:0] rs1,
  output [3:0] rs2,
  output [3:0] rd,
  output out_19,
  output out_20,
  output out_21,
  output [3:0] immed,
  output [3:0] rs1_2,
  output [3:0] rd_2,
  output [3:0] opcode
);

  wire multiplexer_3_out, multiplexer_4_out, not_1_out;
  wire [2:0] multiplexer_1_out, n3_bit_alu_1_b0, register_1_q;
  wire [7:0] n8_bit_alu_2_b0, n8_bit_alu_3_b0, ram_2_data;

  Multiplexer #(.width(3)) multiplexer_1 (
    .in0(in_4), .in1(rd[2:0]), .out(multiplexer_1_out), .sel(opcode[0]));  // open: en
  Multiplexer #(.width(8)) multiplexer_2 (
    .in0(n8_bit_alu_3_b0), .in1(out_15), .out(Write_Input), .sel(opcode[2]));  // open: en
  _3_bit_ALU u_3_bit_alu_1 (
    .A(register_1_q[0]), .in_2(register_1_q[1]), .in_3(register_1_q[2]), .B(multiplexer_1_out[0]),
    .in_5(multiplexer_1_out[1]), .in_6(multiplexer_1_out[2]), .CIN(in_6), .C1(in_9), .C2(in_10),
    .B0(n3_bit_alu_1_b0[0]), .B1(n3_bit_alu_1_b0[1]), .B2(n3_bit_alu_1_b0[2]));
  not not_1 (not_1_out, in_5);
  Register #(.width(3)) register_1 (.D(n3_bit_alu_1_b0), .Q(register_1_q), .clk(in_5));  // open: en, clr
  Register_File register_file_1 (
    .rd(rd), .rs1(rs1), .in_3(immed), .Write_Input(Write_Input), .Enable(in_1), .Clock(not_1_out),
    .out_7(out_12), .out_8(out_14));
  _8_bit_ALU u_8_bit_alu_1 (
    .A(out_12[0]), .in_2(out_12[1]), .in_3(out_12[2]), .in_4(out_12[3]), .in_5(out_12[4]), .in_6(out_12[5]),
    .in_7(out_12[6]), .in_8(out_12[7]), .B(out_14[0]), .in_10(out_14[1]), .in_11(out_14[2]),
    .in_12(out_14[3]), .in_13(out_14[4]), .in_14(out_14[5]), .in_15(out_14[6]), .in_16(out_14[7]),
    .CIN(in_2), .C1(multiplexer_3_out), .C2(multiplexer_3_out), .B0(out_15[0]), .B1(out_15[1]),
    .B2(out_15[2]), .B3(out_15[3]), .B4(out_15[4]), .B5(out_15[5]), .B6(out_15[6]), .B7(out_15[7]));
  RAM #(.addrWidth(3), .dataWidth(16), .bus("asynch")) ram_1 (
    .addr(register_1_q), .data({immed, rs1, rd, opcode}), .ld(in_7));  // open: sel, clr
  Multiplexer multiplexer_3 (.in1(in_8), .out(multiplexer_3_out), .sel(opcode[2]));  // open: in0, en
  _8_bit_ALU u_8_bit_alu_2 (
    .A(out_12[0]), .in_2(out_12[1]), .in_3(out_12[2]), .in_4(out_12[3]), .in_5(out_12[4]), .in_6(out_12[5]),
    .in_7(out_12[6]), .in_8(out_12[7]), .B(immed[0]), .in_10(immed[1]), .in_11(immed[2]), .in_12(immed[3]),
    .in_13(in_3), .in_14(in_3), .in_15(in_3), .in_16(in_3), .CIN(in_3), .C1(in_3), .C2(in_3),
    .B0(n8_bit_alu_2_b0[0]), .B1(n8_bit_alu_2_b0[1]), .B2(n8_bit_alu_2_b0[2]), .B3(n8_bit_alu_2_b0[3]),
    .B4(n8_bit_alu_2_b0[4]), .B5(n8_bit_alu_2_b0[5]), .B6(n8_bit_alu_2_b0[6]), .B7(n8_bit_alu_2_b0[7]));
  RAM #(.bus("separate")) ram_2 (
    .addr(n8_bit_alu_2_b0), .data(ram_2_data), .ld(opcode[1]));  // open: din, str, sel, clk, clr
  _8_bit_ALU u_8_bit_alu_3 (
    .A(ram_2_data[0]), .in_2(ram_2_data[1]), .in_3(ram_2_data[2]), .in_4(ram_2_data[3]),
    .in_5(ram_2_data[4]), .in_6(ram_2_data[5]), .in_7(ram_2_data[6]), .in_8(ram_2_data[7]), .B(immed[0]),
    .in_10(immed[1]), .in_11(immed[2]), .in_12(immed[3]), .in_13(multiplexer_4_out),
    .in_14(multiplexer_4_out), .in_15(multiplexer_4_out), .in_16(multiplexer_4_out), .CIN(multiplexer_4_out),
    .C1(multiplexer_4_out), .C2(multiplexer_4_out), .B0(n8_bit_alu_3_b0[0]), .B1(n8_bit_alu_3_b0[1]),
    .B2(n8_bit_alu_3_b0[2]), .B3(n8_bit_alu_3_b0[3]), .B4(n8_bit_alu_3_b0[4]), .B5(n8_bit_alu_3_b0[5]),
    .B6(n8_bit_alu_3_b0[6]), .B7(n8_bit_alu_3_b0[7]));
  Multiplexer multiplexer_4 (.in1(in_11), .out(multiplexer_4_out), .sel(opcode[1]));  // open: in0, en

  assign out_19 = opcode[0];
  assign out_20 = opcode[1];
  assign out_21 = opcode[2];
  assign rd_2 = rd;
  assign rs1_2 = rs1;
  assign rs2 = immed;

  // Notes on the sheet:
  //   rs1 Output
  //   rs2 Output
  //   immediate for ld
  //   Sum of rs1 and rs2 Outputs
  //   make Instr Memory add imd (5)
  //   turn on load in data memory
  //   turn on add in ALU  (00/10)
endmodule
